// Logisim project rg8.circ as structural Verilog: 29 circuits, main circuit main
module main (
  input  raz,
  output [7:0] s_ir,
  output [3:0] pc,
  output [7:0] e,
  output [7:0] s_out
);

  wire and_1_out, and_2_out, and_3_out, and_4_out, and_5_out, and_6_out, and_7_out, bascule_d_1_qb,
       clock_1_out, commande_1_en_acc, commande_1_en_flag, commande_1_en_ir, commande_1_en_out,
       commande_1_en_pc, commande_1_en_ram, commande_1_hlt, commande_1_saut, commande_1_sub, etapes_1_t0,
       etapes_1_t1, etapes_1_t2, nor_1_out;
  wire [1:0] commande_1_op, commande_1_src;
  wire [3:0] flags_s, ual8_1_z;
  wire [7:0] acc_s, ram16x8_1_dout, rom16x8_1_instr, ual8_1_r;

  Clock clock_1 (.out(clock_1_out));
  pc4 pc4_1 (.load(commande_1_saut), .adr(s_ir[3:0]), .raz(raz), .w(and_3_out), .pc(pc));
  etapes etapes_1 (.clk(and_1_out), .raz(raz), .t1(etapes_1_t1), .t0(etapes_1_t0), .t2(etapes_1_t2));
  rom16x8 rom16x8_1 (.adr(pc), .instr(rom16x8_1_instr));
  commande commande_1 (
    .t0(etapes_1_t0), .t1(etapes_1_t1), .t2(etapes_1_t2), .opcode(s_ir[7:4]), .z(flags_s[0]), .c(flags_s[3]),
    .n(flags_s[1]), .en_ir(commande_1_en_ir), .en_pc(commande_1_en_pc), .en_out(commande_1_en_out),
    .en_ram(commande_1_en_ram), .hlt(commande_1_hlt), .en_acc(commande_1_en_acc), .sub(commande_1_sub),
    .en_flag(commande_1_en_flag), .src(commande_1_src), .op(commande_1_op), .saut(commande_1_saut));
  nor nor_1 (nor_1_out, clock_1_out, raz);
  and and_1 (and_1_out, clock_1_out, bascule_d_1_qb);
  bascule_d bascule_d_1 (.d(1'b0), .clk(1'b0), .raz(raz), .s(commande_1_hlt), .Qb(bascule_d_1_qb));  // open: q
  and and_2 (and_2_out, nor_1_out, commande_1_en_ir);
  and and_3 (and_3_out, nor_1_out, commande_1_en_pc);
  and and_4 (and_4_out, nor_1_out, commande_1_en_acc);
  and and_5 (and_5_out, nor_1_out, commande_1_en_ram);
  and and_6 (and_6_out, nor_1_out, commande_1_en_flag);
  and and_7 (and_7_out, nor_1_out, commande_1_en_out);
  reg8 ir (.e(rom16x8_1_instr), .raz(raz), .w(and_2_out), .r(1'b1), .en(1'b1), .s(s_ir));
  reg8 acc (.e(e), .raz(raz), .w(and_4_out), .r(1'b1), .en(1'b1), .s(acc_s));
  ram16x8 ram16x8_1 (.adr(s_ir[3:0]), .din(acc_s), .raz(raz), .w(and_5_out), .dout(ram16x8_1_dout));
  ual8 ual8_1 (
    .sub(commande_1_sub), .op(commande_1_op), .a(acc_s), .b(ram16x8_1_dout), .r(ual8_1_r), .n(ual8_1_z[1]),
    .z(ual8_1_z[0]), .v(ual8_1_z[2]), .c(ual8_1_z[3]));
  reg8 outt (.e(acc_s), .raz(raz), .w(and_7_out), .r(1'b1), .en(1'b1), .s(s_out));
  mux4_8 mux4_8_1 (
    .e0(ual8_1_r), .e1(ram16x8_1_dout), .e2({4'b0000, s_ir[3:0]}), .e3({8{1'b0}}), .sel(commande_1_src), .s(e));
  reg4 flags (.E(ual8_1_z), .raz(raz), .W(and_6_out), .R(1'b1), .EN(1'b1), .S(flags_s));
endmodule

module add_full (
  input  a,
  input  b,
  input  rin,
  output r_out,
  output s
);

  wire demi_add_1_r, demi_add_1_s, demi_add_2_r;

  demi_add demi_add_1 (.a(a), .b(b), .r(demi_add_1_r), .s(demi_add_1_s));
  xor xor_1 (r_out, demi_add_1_r, demi_add_2_r);
  demi_add demi_add_2 (.a(demi_add_1_s), .b(rin), .r(demi_add_2_r), .s(s));
endmodule

module demi_add (
  input  a,
  input  b,
  output r,
  output s
);

  and and_1 (r, a, b);
  xor xor_1 (s, a, b);
endmodule

module add4 (
  input  a0,
  input  b0,
  input  r_in,
  input  a1,
  input  b1,
  input  a2,
  input  b2,
  input  a3,
  input  b3,
  output s0,
  output s1,
  output s2,
  output r_out,
  output s3
);

  wire add_full_1_r_out, add_full_2_r_out, add_full_3_r_out;

  add_full add_full_1 (.a(a0), .b(b0), .rin(r_in), .r_out(add_full_1_r_out), .s(s0));
  add_full add_full_2 (.a(a1), .b(b1), .rin(add_full_1_r_out), .r_out(add_full_2_r_out), .s(s1));
  add_full add_full_3 (.a(a2), .b(b2), .rin(add_full_2_r_out), .r_out(add_full_3_r_out), .s(s2));
  add_full add_full_4 (.a(a3), .b(b3), .rin(add_full_3_r_out), .r_out(r_out), .s(s3));
endmodule

module add8 (
  input  a0,
  input  b0,
  input  in_3,
  input  a1,
  input  b1,
  input  a2,
  input  b2,
  input  a3,
  input  b3,
  input  a4,
  input  b4,
  input  a5,
  input  b5,
  input  a6,
  input  b6,
  input  a7,
  input  b7,
  output [7:0] out_18,
  output out_19
);

  wire add4_1_r_out;

  add4 add4_1 (
    .a0(a0), .b0(b0), .r_in(in_3), .a1(a1), .b1(b1), .a2(a2), .b2(b2), .a3(a3), .b3(b3), .s0(out_18[0]),
    .s1(out_18[1]), .s2(out_18[2]), .r_out(add4_1_r_out), .s3(out_18[3]));
  add4 add4_2 (
    .a0(a4), .b0(b4), .r_in(add4_1_r_out), .a1(a5), .b1(b5), .a2(a6), .b2(b6), .a3(a7), .b3(b7),
    .s0(out_18[4]), .s1(out_18[5]), .s2(out_18[6]), .r_out(out_19), .s3(out_18[7]));
endmodule

module addsub8 (
  input  [7:0] a,
  input  [7:0] b,
  input  sub,
  output [7:0] s,
  output cout
);

  wire xor_1_out, xor_2_out, xor_3_out, xor_4_out, xor_5_out, xor_6_out, xor_7_out, xor_8_out;

  xor xor_1 (xor_1_out, b[0], sub);
  xor xor_2 (xor_2_out, b[1], sub);
  xor xor_3 (xor_3_out, b[2], sub);
  xor xor_4 (xor_4_out, b[3], sub);
  xor xor_5 (xor_5_out, b[4], sub);
  xor xor_6 (xor_6_out, b[5], sub);
  xor xor_7 (xor_7_out, b[6], sub);
  xor xor_8 (xor_8_out, b[7], sub);
  add8 add8_1 (
    .a0(sub), .b0(a[0]), .in_3(xor_1_out), .a1(a[1]), .b1(xor_2_out), .a2(a[2]), .b2(xor_3_out), .a3(a[3]),
    .b3(xor_4_out), .a4(a[4]), .b4(xor_5_out), .a5(a[5]), .b5(xor_6_out), .a6(a[6]), .b6(xor_7_out),
    .a7(a[7]), .b7(xor_8_out), .out_18(s), .out_19(cout));
endmodule

module dec2_4 (
  input  e0,
  input  e1,
  output s3,
  output s2,
  output s1,
  output s0
);

  wire not_1_out, not_2_out;

  not not_1 (not_1_out, e0);
  not not_2 (not_2_out, e1);
  and and_1 (s3, e0, e1);
  and and_2 (s2, e0, not_2_out);
  and and_3 (s1, not_1_out, e1);
  and and_4 (s0, not_1_out, not_2_out);
endmodule

module dec4_16 (
  input  [3:0] a,
  output [15:0] s
);

  wire dec2_4_1_s0, dec2_4_1_s1, dec2_4_1_s2, dec2_4_1_s3, dec2_4_2_s0, dec2_4_2_s1, dec2_4_2_s2, dec2_4_2_s3;

  dec2_4 dec2_4_1 (.e0(a[1]), .e1(a[0]), .s3(dec2_4_1_s3), .s2(dec2_4_1_s2), .s1(dec2_4_1_s1), .s0(dec2_4_1_s0));
  dec2_4 dec2_4_2 (.e0(a[3]), .e1(a[2]), .s3(dec2_4_2_s3), .s2(dec2_4_2_s2), .s1(dec2_4_2_s1), .s0(dec2_4_2_s0));
  and and_1 (s[0], dec2_4_2_s0, dec2_4_1_s0);
  and and_2 (s[1], dec2_4_2_s0, dec2_4_1_s1);
  and and_3 (s[2], dec2_4_2_s0, dec2_4_1_s2);
  and and_4 (s[3], dec2_4_2_s0, dec2_4_1_s3);
  and and_5 (s[4], dec2_4_2_s1, dec2_4_1_s0);
  and and_6 (s[5], dec2_4_2_s1, dec2_4_1_s1);
  and and_7 (s[6], dec2_4_2_s1, dec2_4_1_s2);
  and and_8 (s[7], dec2_4_2_s1, dec2_4_1_s3);
  and and_9 (s[8], dec2_4_2_s2, dec2_4_1_s0);
  and and_10 (s[9], dec2_4_2_s2, dec2_4_1_s1);
  and and_11 (s[10], dec2_4_2_s2, dec2_4_1_s2);
  and and_12 (s[11], dec2_4_2_s2, dec2_4_1_s3);
  and and_13 (s[12], dec2_4_2_s3, dec2_4_1_s0);
  and and_14 (s[13], dec2_4_2_s3, dec2_4_1_s1);
  and and_15 (s[14], dec2_4_2_s3, dec2_4_1_s2);
  and and_16 (s[15], dec2_4_2_s3, dec2_4_1_s3);
endmodule

module mux4 (
  input  a2,
  input  a1,
  input  e3,
  input  e2,
  input  e1,
  input  e0,
  output s
);

  wire and_1_out, and_2_out, and_3_out, and_4_out, dec2_4_1_s0, dec2_4_1_s1, dec2_4_1_s2, dec2_4_1_s3;

  dec2_4 dec2_4_1 (.e0(a1), .e1(a2), .s3(dec2_4_1_s3), .s2(dec2_4_1_s2), .s1(dec2_4_1_s1), .s0(dec2_4_1_s0));
  and and_1 (and_1_out, e3, dec2_4_1_s3);
  and and_2 (and_2_out, e2, dec2_4_1_s2);
  and and_3 (and_3_out, e1, dec2_4_1_s1);
  and and_4 (and_4_out, e0, dec2_4_1_s0);
  or or_1 (s, and_1_out, and_2_out, and_3_out, and_4_out);
endmodule

module mux4_8 (
  input  [7:0] e0,
  input  [7:0] e1,
  input  [7:0] e2,
  input  [7:0] e3,
  input  [1:0] sel,
  output [7:0] s
);

  mux4 mux4_1 (.a2(sel[0]), .a1(sel[1]), .e3(e3[0]), .e2(e2[0]), .e1(e1[0]), .e0(e0[0]), .s(s[0]));
  mux4 mux4_2 (.a2(sel[0]), .a1(sel[1]), .e3(e3[1]), .e2(e2[1]), .e1(e1[1]), .e0(e0[1]), .s(s[1]));
  mux4 mux4_3 (.a2(sel[0]), .a1(sel[1]), .e3(e3[2]), .e2(e2[2]), .e1(e1[2]), .e0(e0[2]), .s(s[2]));
  mux4 mux4_4 (.a2(sel[0]), .a1(sel[1]), .e3(e3[3]), .e2(e2[3]), .e1(e1[3]), .e0(e0[3]), .s(s[3]));
  mux4 mux4_5 (.a2(sel[0]), .a1(sel[1]), .e3(e3[4]), .e2(e2[4]), .e1(e1[4]), .e0(e0[4]), .s(s[4]));
  mux4 mux4_6 (.a2(sel[0]), .a1(sel[1]), .e3(e3[5]), .e2(e2[5]), .e1(e1[5]), .e0(e0[5]), .s(s[5]));
  mux4 mux4_7 (.a2(sel[0]), .a1(sel[1]), .e3(e3[6]), .e2(e2[6]), .e1(e1[6]), .e0(e0[6]), .s(s[6]));
  mux4 mux4_8 (.a2(sel[0]), .a1(sel[1]), .e3(e3[7]), .e2(e2[7]), .e1(e1[7]), .e0(e0[7]), .s(s[7]));
endmodule

module mux16_8 (
  input  [7:0] e0,
  input  [7:0] e1,
  input  [7:0] e2,
  input  [7:0] e3,
  input  [7:0] e4,
  input  [7:0] e5,
  input  [7:0] e6,
  input  [7:0] e7,
  input  [7:0] e8,
  input  [7:0] e9,
  input  [7:0] e10,
  input  [7:0] e11,
  input  [7:0] e12,
  input  [7:0] e13,
  input  [7:0] e14,
  input  [7:0] e15,
  input  [3:0] sel,
  output [7:0] s
);

  wire [7:0] mux4_8_1_s, mux4_8_2_s, mux4_8_3_s, mux4_8_4_s;

  mux4_8 mux4_8_1 (.e0(e0), .e1(e1), .e2(e2), .e3(e3), .sel(sel[1:0]), .s(mux4_8_1_s));
  mux4_8 mux4_8_2 (.e0(e4), .e1(e5), .e2(e6), .e3(e7), .sel(sel[1:0]), .s(mux4_8_2_s));
  mux4_8 mux4_8_3 (.e0(e8), .e1(e9), .e2(e10), .e3(e11), .sel(sel[1:0]), .s(mux4_8_3_s));
  mux4_8 mux4_8_4 (.e0(e12), .e1(e13), .e2(e14), .e3(e15), .sel(sel[1:0]), .s(mux4_8_4_s));
  mux4_8 mux4_8_5 (.e0(mux4_8_1_s), .e1(mux4_8_2_s), .e2(mux4_8_3_s), .e3(mux4_8_4_s), .sel(sel[3:2]), .s(s));
endmodule

module ual8 (
  input  [7:0] a,
  input  [7:0] b,
  input  [1:0] op,
  input  sub,
  output v,
  output [7:0] r,
  output c,
  output z,
  output n
);

  wire not_2_out, xor_1_out, xor_2_out, xor_3_out;
  wire [7:0] addsub8_1_s, and_1_out, not_1_out, or_1_out;

  assign and_1_out = a & b;  // AND_Gate and_1, 8 bits wide
  assign or_1_out = a | b;  // OR_Gate or_1, 8 bits wide
  assign not_1_out = ~a;  // NOT_Gate not_1, 8 bits wide
  addsub8 addsub8_1 (.a(a), .b(b), .sub(sub), .s(addsub8_1_s), .cout(c));
  mux4_8 mux4_8_1 (.e0(addsub8_1_s), .e1(and_1_out), .e2(or_1_out), .e3(not_1_out), .sel(op), .s({n, r[6:0]}));
  nor nor_1 (z, r[0], r[1], r[2], r[3], r[4], r[5], r[6], n);
  xor xor_1 (xor_1_out, b[7], sub);
  xor xor_2 (xor_2_out, a[7], n);
  xor xor_3 (xor_3_out, xor_1_out, a[7]);
  not not_2 (not_2_out, xor_3_out);
  and and_2 (v, xor_2_out, not_2_out);

  assign r[7] = n;
endmodule

module verrou_d (
  input  d,
  input  en,
  input  s,
  input  raz,
  output q,
  output Qb
);

  wire nand_1_out, nand_2_out, not_1_out, not_2_out, not_3_out;

  not not_1 (not_1_out, d);
  not not_2 (not_2_out, s);
  nand nand_1 (nand_1_out, d, not_3_out, en);
  nand nand_2 (nand_2_out, not_1_out, not_2_out, en);
  nand nand_3 (Qb, q, not_3_out, nand_2_out);
  not not_3 (not_3_out, raz);
  nand nand_4 (q, nand_1_out, not_2_out, Qb);
endmodule

module bascule_d (
  input  d,
  input  clk,
  input  raz,
  input  s,
  output q,
  output Qb
);

  wire not_1_out, verrou_d_1_q;

  not not_1 (not_1_out, clk);
  verrou_d verrou_d_1 (.d(d), .en(not_1_out), .s(s), .raz(raz), .q(verrou_d_1_q));  // open: Qb
  verrou_d verrou_d_2 (.d(verrou_d_1_q), .en(clk), .s(s), .raz(raz), .Qb(Qb), .q(q));
endmodule

module reg1 (
  input  E,
  input  raz,
  input  W,
  input  R,
  input  EN,
  output S
);

  wire and_1_out, bascule_d_1_q;

  and and_1 (and_1_out, W, EN);
  bascule_d bascule_d_1 (.d(E), .clk(and_1_out), .raz(raz), .s(1'b0), .q(bascule_d_1_q));  // open: Qb
  and and_2 (S, bascule_d_1_q, R, EN);
endmodule

module reg4 (
  input  [3:0] E,
  input  raz,
  input  W,
  input  R,
  input  EN,
  output [3:0] S
);

  reg1 reg1_1 (.EN(EN), .W(W), .E(E[0]), .raz(raz), .R(R), .S(S[0]));
  reg1 reg1_2 (.EN(EN), .W(W), .E(E[1]), .raz(raz), .R(R), .S(S[1]));
  reg1 reg1_3 (.EN(EN), .W(W), .E(E[2]), .raz(raz), .R(R), .S(S[2]));
  reg1 reg1_4 (.EN(EN), .W(W), .E(E[3]), .raz(raz), .R(R), .S(S[3]));
endmodule

module reg8 (
  input  [7:0] e,
  input  raz,
  input  w,
  input  r,
  input  en,
  output [7:0] s
);

  reg4 reg4_1 (.E(e[3:0]), .raz(raz), .W(w), .R(r), .EN(en), .S(s[3:0]));
  reg4 reg4_2 (.E(e[7:4]), .raz(raz), .W(w), .R(r), .EN(en), .S(s[7:4]));
endmodule

module ram16x8 (
  input  [3:0] adr,
  input  w,
  input  [7:0] din,
  input  raz,
  output [7:0] dout
);

  wire [7:0] reg8_1_s, reg8_2_s, reg8_3_s, reg8_4_s, reg8_5_s, reg8_6_s, reg8_7_s, reg8_8_s, reg8_9_s,
       reg8_10_s, reg8_11_s, reg8_12_s, reg8_13_s, reg8_14_s, reg8_15_s, reg8_16_s;
  wire [15:0] dec4_16_1_s;

  dec4_16 dec4_16_1 (.a(adr), .s(dec4_16_1_s));
  mux16_8 mux16_8_1 (
    .e0(reg8_1_s), .e1(reg8_2_s), .e2(reg8_3_s), .e3(reg8_4_s), .e4(reg8_5_s), .e5(reg8_6_s), .e6(reg8_7_s),
    .e7(reg8_8_s), .e8(reg8_9_s), .e9(reg8_10_s), .e10(reg8_11_s), .e11(reg8_12_s), .e12(reg8_13_s),
    .e13(reg8_14_s), .e14(reg8_15_s), .e15(reg8_16_s), .sel(adr), .s(dout));
  reg8 reg8_1 (.e(din), .raz(raz), .w(w), .r(1'b1), .en(dec4_16_1_s[0]), .s(reg8_1_s));
  reg8 reg8_2 (.e(din), .raz(raz), .w(w), .r(1'b1), .en(dec4_16_1_s[1]), .s(reg8_2_s));
  reg8 reg8_3 (.e(din), .raz(raz), .w(w), .r(1'b1), .en(dec4_16_1_s[2]), .s(reg8_3_s));
  reg8 reg8_4 (.e(din), .raz(raz), .w(w), .r(1'b1), .en(dec4_16_1_s[3]), .s(reg8_4_s));
  reg8 reg8_5 (.e(din), .raz(raz), .w(w), .r(1'b1), .en(dec4_16_1_s[4]), .s(reg8_5_s));
  reg8 reg8_6 (.e(din), .raz(raz), .w(w), .r(1'b1), .en(dec4_16_1_s[5]), .s(reg8_6_s));
  reg8 reg8_7 (.e(din), .raz(raz), .w(w), .r(1'b1), .en(dec4_16_1_s[6]), .s(reg8_7_s));
  reg8 reg8_8 (.e(din), .raz(raz), .w(w), .r(1'b1), .en(dec4_16_1_s[7]), .s(reg8_8_s));
  reg8 reg8_9 (.e(din), .raz(raz), .w(w), .r(1'b1), .en(dec4_16_1_s[8]), .s(reg8_9_s));
  reg8 reg8_10 (.e(din), .raz(raz), .w(w), .r(1'b1), .en(dec4_16_1_s[9]), .s(reg8_10_s));
  reg8 reg8_11 (.e(din), .raz(raz), .w(w), .r(1'b1), .en(dec4_16_1_s[10]), .s(reg8_11_s));
  reg8 reg8_12 (.e(din), .raz(raz), .w(w), .r(1'b1), .en(dec4_16_1_s[11]), .s(reg8_12_s));
  reg8 reg8_13 (.e(din), .raz(raz), .w(w), .r(1'b1), .en(dec4_16_1_s[12]), .s(reg8_13_s));
  reg8 reg8_14 (.e(din), .raz(raz), .w(w), .r(1'b1), .en(dec4_16_1_s[13]), .s(reg8_14_s));
  reg8 reg8_15 (.e(din), .raz(raz), .w(w), .r(1'b1), .en(dec4_16_1_s[14]), .s(reg8_15_s));
  reg8 reg8_16 (.e(din), .raz(raz), .w(w), .r(1'b1), .en(dec4_16_1_s[15]), .s(reg8_16_s));
endmodule

module cpt3_logique (
  input  Q0,
  input  Q1,
  input  Q2,
  output D0,
  output D1,
  output D2
);

  wire and_1_out, and_2_out, and_3_out, and_4_out, not_1_out, not_2_out;

  not not_1 (not_1_out, Q0);
  not not_2 (not_2_out, Q1);
  not not_3 (D2, Q2);
  and and_1 (and_1_out, Q1, Q2);
  or or_1 (D0, and_1_out, and_2_out);
  and and_2 (and_2_out, Q0, D2);
  and and_3 (and_3_out, not_1_out, not_2_out, Q2);
  or or_2 (D1, and_3_out, and_4_out);
  and and_4 (and_4_out, Q1, D2);
endmodule

module cpt3_load (
  input  clk,
  input  [2:0] E,
  input  loadd,
  output [2:0] out_4
);

  wire and_1_out, and_2_out, and_3_out, and_4_out, and_5_out, and_6_out, cpt3_logique_1_d1, not_1_out,
       not_2_out, not_3_out, undriven;

  bascule_d bascule_d_1 (.d(undriven), .clk(clk), .raz(and_1_out), .s(and_2_out), .q(out_4[2]));  // open: Qb
  bascule_d bascule_d_2 (.d(undriven), .clk(clk), .raz(and_5_out), .s(and_6_out), .q(out_4[0]));  // open: Qb
  and and_1 (and_1_out, not_1_out, loadd);
  not not_1 (not_1_out, E[2]);
  and and_2 (and_2_out, E[2], loadd);
  and and_3 (and_3_out, not_2_out, loadd);
  not not_2 (not_2_out, E[1]);
  cpt3_logique cpt3_logique_1 (.Q0(out_4[2]), .Q1(out_4[1]), .Q2(out_4[0]), .D1(cpt3_logique_1_d1));  // open: D0, D2
  and and_4 (and_4_out, E[1], loadd);
  and and_5 (and_5_out, not_3_out, loadd);
  not not_3 (not_3_out, E[0]);
  bascule_d bascule_d_3 (.d(cpt3_logique_1_d1), .clk(clk), .raz(and_3_out), .s(and_4_out), .q(out_4[1]));  // open: Qb
  and and_6 (and_6_out, E[0], loadd);
endmodule

module seg7_dec (
  input  e3,
  input  e2,
  input  e1,
  input  e0,
  output a,
  output b,
  output c,
  output d,
  output e,
  output f,
  output g
);

  wire and_1_out, and_2_out, and_3_out, and_4_out, and_5_out, and_6_out, and_7_out, and_8_out, and_9_out,
       and_10_out, and_11_out, and_12_out, and_13_out, and_14_out, and_15_out, and_16_out, not_1_out,
       not_2_out, not_3_out;

  not not_1 (not_1_out, e2);
  not not_2 (not_2_out, e1);
  not not_3 (not_3_out, e0);
  and and_1 (and_1_out, not_1_out, not_3_out);
  and and_2 (and_2_out, e2, e0);
  and and_3 (and_3_out, not_2_out, not_3_out);
  and and_4 (and_4_out, e1, e0);
  or or_1 (c, not_2_out, e0, e2);
  and and_5 (and_5_out, not_1_out, not_3_out);
  and and_6 (and_6_out, not_1_out, e1);
  and and_7 (and_7_out, e2, not_2_out, e0);
  and and_8 (and_8_out, e1, not_3_out);
  and and_9 (and_9_out, not_1_out, not_3_out);
  and and_10 (and_10_out, e1, not_3_out);
  and and_11 (and_11_out, not_2_out, not_3_out);
  and and_12 (and_12_out, e2, not_2_out);
  and and_13 (and_13_out, e2, not_3_out);
  and and_14 (and_14_out, not_1_out, e1);
  and and_15 (and_15_out, e2, not_2_out);
  and and_16 (and_16_out, e1, not_3_out);
  or or_2 (a, and_1_out, e1, and_2_out, e3);
  or or_3 (b, not_1_out, and_3_out, and_4_out);
  or or_4 (d, and_5_out, and_6_out, and_7_out, and_8_out, e3);
  or or_5 (e, and_9_out, and_10_out);
  or or_6 (f, and_11_out, and_12_out, and_13_out, e3);
  or or_7 (g, and_14_out, and_15_out, e3, and_16_out);
endmodule

module seg7_hex (
  input  e3,
  input  e2,
  input  e1,
  input  e0,
  output a,
  output b,
  output c,
  output d,
  output e,
  output f,
  output g
);

  wire and_1_out, and_2_out, and_3_out, and_4_out, and_5_out, and_6_out, and_7_out, and_8_out, and_9_out,
       and_10_out, and_11_out, and_12_out, and_13_out, and_14_out, and_15_out, and_16_out, and_17_out,
       and_18_out, and_19_out, and_20_out, and_21_out, and_22_out, and_23_out, and_24_out, and_25_out,
       and_26_out, and_27_out, and_28_out, and_29_out, and_30_out, and_31_out, and_32_out, and_33_out,
       and_34_out, and_35_out, and_36_out, and_37_out, and_38_out, and_39_out, and_40_out, not_1_out,
       not_2_out, not_3_out, not_4_out;

  not not_1 (not_1_out, e3);
  not not_2 (not_2_out, e2);
  not not_3 (not_3_out, e1);
  not not_4 (not_4_out, e0);
  and and_1 (and_1_out, not_2_out, not_4_out);
  and and_2 (and_2_out, not_1_out, e1);
  and and_3 (and_3_out, not_1_out, e2, e0);
  and and_4 (and_4_out, e3, not_2_out, not_3_out);
  and and_5 (and_5_out, e3, not_4_out);
  and and_6 (and_6_out, e2, e1);
  and and_7 (and_7_out, not_1_out, not_3_out, not_4_out);
  and and_8 (and_8_out, not_1_out, e1, e0);
  and and_9 (and_9_out, not_2_out, not_4_out);
  and and_10 (and_10_out, e3, not_3_out, e0);
  and and_11 (and_11_out, not_1_out, not_2_out);
  and and_12 (and_12_out, not_1_out, e2);
  and and_13 (and_13_out, e3, not_2_out);
  and and_14 (and_14_out, not_3_out, e0);
  and and_15 (and_15_out, not_1_out, not_3_out);
  and and_16 (and_16_out, not_1_out, e0);
  and and_17 (and_17_out, e2, not_3_out, e0);
  and and_18 (and_18_out, not_1_out, not_2_out, not_4_out);
  and and_19 (and_19_out, not_1_out, not_2_out, e1);
  and and_20 (and_20_out, not_1_out, e1, not_4_out);
  and and_21 (and_21_out, not_2_out, not_3_out, not_4_out);
  and and_22 (and_22_out, e3, not_2_out, e0);
  and and_23 (and_23_out, e3, not_3_out);
  and and_24 (and_24_out, e2, e1, not_4_out);
  and and_25 (and_25_out, not_2_out, not_4_out);
  and and_26 (and_26_out, e1, not_4_out);
  and and_27 (and_27_out, e3, e1);
  and and_28 (and_28_out, e3, e2);
  and and_29 (and_29_out, not_3_out, not_4_out);
  and and_30 (and_30_out, not_1_out, e2, not_3_out);
  and and_31 (and_31_out, e2, not_4_out);
  and and_32 (and_32_out, e3, not_2_out);
  and and_33 (and_33_out, e3, e1);
  and and_34 (and_34_out, not_2_out, e1);
  and and_35 (and_35_out, e3, not_2_out);
  and and_36 (and_36_out, not_1_out, e2, not_3_out);
  and and_37 (and_37_out, not_1_out, e2, not_4_out);
  and and_38 (and_38_out, e2, not_3_out, e0);
  and and_39 (and_39_out, e1, not_4_out);
  and and_40 (and_40_out, e3, e0);
  or or_1 (a, and_1_out, and_2_out, and_3_out, and_4_out, and_5_out, and_6_out);
  or or_2 (b, and_7_out, and_8_out, and_9_out, and_10_out, and_11_out);
  or or_3 (c, and_12_out, and_13_out, and_14_out, and_15_out, and_16_out);
  or or_4 (d, and_17_out, and_18_out, and_19_out, and_20_out, and_21_out, and_22_out, and_23_out, and_24_out);
  or or_5 (e, and_25_out, and_26_out, and_27_out, and_28_out);
  or or_6 (f, and_29_out, and_30_out, and_31_out, and_32_out, and_33_out);
  or or_7 (g, and_34_out, and_35_out, and_36_out, and_37_out, and_38_out, and_39_out, and_40_out);
endmodule

module byte_to_bcd (
  input  [7:0] E,
  output [3:0] c,
  output [3:0] d,
  output [3:0] u
);

  wire [7:0] divider_1_out;
  wire [7:4] divider_1_rem, divider_2_out, divider_2_rem;

  Divider divider_1 (.a(E), .b(8'ha), .out(divider_1_out), .rem({divider_1_rem, u}));  // open: upper
  Divider divider_2 (.a(divider_1_out), .b(8'ha), .out({divider_2_out, c}), .rem({divider_2_rem, d}));  // open: upper
endmodule

module pc4 (
  input  load,
  input  raz,
  input  w,
  input  [3:0] adr,
  output [3:0] pc
);

  wire [3:0] add4_1_s0, mux2_4_1_s;

  reg4 reg4_1 (.E(mux2_4_1_s), .raz(raz), .W(w), .R(1'b1), .EN(1'b1), .S(pc));
  mux2_4 mux2_4_1 (.e1(adr), .e0(add4_1_s0), .sel(load), .s(mux2_4_1_s));
  add4 add4_1 (
    .a0(pc[0]), .b0(1'b1), .r_in(1'b0), .a1(pc[1]), .b1(1'b0), .a2(pc[2]), .b2(1'b0), .a3(pc[3]), .b3(1'b0),
    .s0(add4_1_s0[0]), .s1(add4_1_s0[1]), .s2(add4_1_s0[2]), .s3(add4_1_s0[3]));  // open: r_out
endmodule

module mux2 (
  input  e1,
  input  sel,
  input  e0,
  output s
);

  wire and_1_out, and_2_out, not_1_out;

  not not_1 (not_1_out, sel);
  and and_1 (and_1_out, e1, sel);
  and and_2 (and_2_out, not_1_out, e0);
  or or_1 (s, and_1_out, and_2_out);
endmodule

module mux2_4 (
  input  [3:0] e1,
  input  [3:0] e0,
  input  sel,
  output [3:0] s
);

  mux2 mux2_1 (.e1(e1[0]), .sel(sel), .e0(e0[0]), .s(s[0]));
  mux2 mux2_2 (.e1(e1[1]), .sel(sel), .e0(e0[1]), .s(s[1]));
  mux2 mux2_3 (.e1(e1[2]), .sel(sel), .e0(e0[2]), .s(s[2]));
  mux2 mux2_4 (.e1(e1[3]), .sel(sel), .e0(e0[3]), .s(s[3]));
endmodule

module rom16x8 (
  input  [3:0] adr,
  output [7:0] instr
);

  mux16_8 mux16_8_1 (
    .e0(8'h25), .e1(8'h3f), .e2(8'h23), .e3(8'h4f), .e4(8'he0), .e5(8'hf0), .e6({8{1'b0}}), .e7({8{1'b0}}),
    .e8({8{1'b0}}), .e9({8{1'b0}}), .e10({8{1'b0}}), .e11({8{1'b0}}), .e12({8{1'b0}}), .e13({8{1'b0}}),
    .e14({8{1'b0}}), .e15({8{1'b0}}), .sel(adr), .s(instr));
endmodule

module etapes (
  input  clk,
  input  raz,
  output t1,
  output t0,
  output t2
);

  bascule_d bascule_d_1 (.d(t0), .clk(clk), .raz(raz), .s(1'b0), .q(t1));  // open: Qb
  bascule_d bascule_d_2 (.d(t1), .clk(clk), .raz(raz), .s(1'b0), .q(t2));  // open: Qb
  nor nor_1 (t0, t1, t2);
endmodule

module commande (
  input  t0,
  input  t1,
  input  t2,
  input  [3:0] opcode,
  input  z,
  input  c,
  input  n,
  output en_ir,
  output en_pc,
  output en_out,
  output en_ram,
  output hlt,
  output en_acc,
  output sub,
  output en_flag,
  output [1:0] src,
  output [1:0] op,
  output saut
);

  wire and_1_out, and_2_out, and_3_out, or_2_out, or_3_out;
  wire [15:0] dec4_16_1_s;

  and and_1 (and_1_out, n, dec4_16_1_s[12]);
  dec4_16 dec4_16_1 (.a(opcode), .s({dec4_16_1_s[15:6], sub, dec4_16_1_s[4:3], src, dec4_16_1_s[0]}));
  and and_2 (and_2_out, c, dec4_16_1_s[11]);
  or or_1 (saut, and_1_out, and_2_out, and_3_out, dec4_16_1_s[9]);
  and and_3 (and_3_out, z, dec4_16_1_s[10]);
  or or_2 (or_2_out, src[0], src[1], dec4_16_1_s[8], dec4_16_1_s[4], sub, dec4_16_1_s[6], dec4_16_1_s[7]);
  or or_3 (or_3_out, dec4_16_1_s[4], sub, dec4_16_1_s[6], dec4_16_1_s[7], dec4_16_1_s[8]);
  and and_4 (en_flag, or_3_out, t1);
  or or_4 (op[0], dec4_16_1_s[6], dec4_16_1_s[8]);
  or or_5 (op[1], dec4_16_1_s[8], dec4_16_1_s[7]);
  and and_5 (en_out, t1, dec4_16_1_s[14]);
  and and_6 (en_ram, t1, dec4_16_1_s[3]);
  and and_7 (hlt, t1, dec4_16_1_s[15]);
  and and_8 (en_acc, or_2_out, t1);

  assign en_ir = t0;
  assign en_pc = t2;
endmodule
